// Logisim project 3_CodyTodd.circ as structural Verilog: 1 circuit, main circuit main
module main (
  input  in_1,
  input  in_2,
  input  Cin,
  input  in_4,
  input  in_5,
  input  in_6,
  input  in_7,
  input  in_8,
  input  in_9,
  input  in_10,
  input  in_11,
  output Sum,
  output Cout,
  output sum0,
  output sum1,
  output sum2,
  output sum3,
  output Carry
);

  wire and_1_out, and_2_out, and_3_out, and_4_out, and_5_out, and_6_out, and_7_out, and_8_out, and_9_out,
       or_2_out, or_3_out, xor_1_out, xor_3_out, xor_4_out, xor_5_out;

  xor xor_1 (xor_1_out, in_1, in_2);
  xor xor_2 (sum0, in_4, in_5);
  and and_1 (and_1_out, in_4, in_5);
  xor xor_3 (xor_3_out, in_6, in_7);
  and and_2 (and_2_out, in_6, in_7);
  xor xor_4 (xor_4_out, in_8, in_9);
  and and_3 (and_3_out, in_8, in_9);
  xor xor_5 (xor_5_out, in_10, in_11);
  and and_4 (and_4_out, in_10, in_11);
  and and_5 (and_5_out, xor_1_out, Cin);
  and and_6 (and_6_out, in_1, in_2);
  xor xor_6 (Sum, xor_1_out, Cin);
  or or_1 (Cout, and_5_out, and_6_out);
  xor xor_7 (sum1, xor_3_out, and_1_out);
  and and_7 (and_7_out, xor_3_out, and_1_out);
  xor xor_8 (sum2, xor_4_out, or_2_out);
  and and_8 (and_8_out, xor_4_out, or_2_out);
  xor xor_9 (sum3, xor_5_out, or_3_out);
  and and_9 (and_9_out, xor_5_out, or_3_out);
  or or_2 (or_2_out, and_7_out, and_2_out);
  or or_3 (or_3_out, and_8_out, and_3_out);
  or or_4 (Carry, and_9_out, and_4_out);

  // Notes on the sheet:
  //   A
  //   B
endmodule
