// Logisim project 4_CodyTodd.circ as structural Verilog: 1 circuit, main circuit main
module main (
  input  in_1,
  input  in_2,
  input  in_3,
  output out_4,
  output out_5
);

  wire adder_1_out, and_1_out, decoder_1_out0, decoder_2_out0, not_1_out, not_2_out, or_1_out;

  not not_1 (not_1_out, in_2);
  not not_2 (not_2_out, in_3);
  Decoder decoder_1 (.out0(decoder_1_out0), .sel(in_2), .en(not_1_out));  // open: out1
  Decoder decoder_2 (.out0(decoder_2_out0), .sel(in_3), .en(not_2_out));  // open: out1
  and and_1 (and_1_out, decoder_1_out0, decoder_2_out0);
  or or_1 (or_1_out, decoder_1_out0, decoder_2_out0);
  Adder #(.width(1)) adder_1 (.a(decoder_1_out0), .b(decoder_2_out0), .out(adder_1_out), .cin(in_1), .cout(out_5));
  Multiplexer #(.select(2)) multiplexer_1 (
    .in0(and_1_out), .in1(or_1_out), .in2(adder_1_out), .out(out_4));  // open: in3, sel
endmodule
