// Logisim project 5_CodyTodd.circ as structural Verilog: 1 circuit, main circuit main
module main (
  input  in_1,
  input  in_2,
  input  in_3,
  output out_4,
  output out_5,
  output out_6,
  output out_7
);

  wire clock_1_out, nand_1_out, nand_2_out, nand_3_out;

  Clock clock_1 (.out(clock_1_out));
  nand nand_1 (nand_1_out, in_3, in_3);
  nor nor_1 (out_4, in_1, out_5);
  nor nor_2 (out_5, out_4, in_2);
  nand nand_2 (nand_2_out, in_3, clock_1_out);
  nand nand_3 (nand_3_out, clock_1_out, nand_1_out);
  nand nand_4 (out_6, nand_2_out, out_7);
  nand nand_5 (out_7, out_6, nand_3_out);
endmodule
